# Fritzing sketch LoopingLouie (saved by Fritzing 0.9.3b)
breadboards: 1

parts:
  S1 = H-Bridge with L298N
  VCC1 = Battery block 9V
  Bauteil1 = Arduino Uno (Rev3) - ICSP
  C1 = Capacitor Polarized [package=panasonic_c]
  S2 = Pushbutton [package="[THT]"]
  S3 = Pushbutton [package="[THT]"]
  S4 = Pushbutton [package="[THT]"]
  S5 = Pushbutton [package="[THT]"]
  M1 = DC Motor
  D2 = Diode [package=diode-hv]
  D3 = Diode [package=diode-hv]
  D4 = Diode [package=diode-hv]
  D5 = Diode [package=diode-hv]

nets:
  N1: S1.12V, VCC1.+, D2.C, D3.C
  GND: S1.GND, VCC1.-, Bauteil1.GND, C1.-
  5V: S1.5V, Bauteil1.VIN
  N2: S1.ENA, Bauteil1.D9_PWM
  N3: S1.IN1, Bauteil1.D7
  N4: S1.IN2, Bauteil1.D8
  N5: S1.M1-01, M1.pin_1, D5.C
  N6: S1.M1-02, S1.M2-01
  N7: Bauteil1.5V, Bauteil1.D2, Bauteil1.D3_PWM, Bauteil1.D4, Bauteil1.D5_PWM, C1.+, S2.Pin_1, S2.Pin_2, S2.Pin_3, S2.Pin_4, S3.Pin_1, S3.Pin_2, S3.Pin_3, S3.Pin_4, S4.Pin_1, S4.Pin_2, S4.Pin_3, S4.Pin_4, S5.Pin_1, S5.Pin_2, S5.Pin_3, S5.Pin_4
  N8: M1.pin_2, D4.C

notes:
  Buttons for the Players
  Capacitor against resetting
  Flyback diodes

custom parts:
  H-Bridge with L298N: h-bridge
